# Fritzing sketch pool-pi_v2 (saved by Fritzing 0.9.9b)

parts:
  MCU1 = Raspberry Pi Zero
  M1 = RioRand LM2596
  J1 = Camdenboss CTB0158-4 [part_number=CTB0158-4 package=THT]
  RS485_module = RS485 Module (MAX3485)

nets:
  N1: MCU1.pin_2, MCU1.pin_4, M1.Pin_3, RS485_module.VCC
  N2: MCU1.pin_8, RS485_module.DI
  N3: MCU1.pin_9, M1.Pin_2, M1.Pin_4, J1.pin4, RS485_module.GND
  N4: MCU1.pin_10, RS485_module.RO
  N5: MCU1.pin_11, RS485_module.RE, RS485_module.DE
  N6: M1.Pin_1, J1.pin1
  N7: J1.pin2, RS485_module.A
  N8: J1.pin3, RS485_module.B

notes:
  RED 1
  BLK 2
  YEL 3
  GRN 4

custom parts:
  RS485 Module (MAX3485): Commercially available RS485 to RS232 TTL Module
